// Logisim project sevenSegmentDisplay.circ as structural Verilog: 8 circuits, main circuit main
module main (
  input  A,
  input  B,
  input  C,
  input  D
);

  wire circuit_a_1_out_5, circuit_b_1_out_5, circuit_c_1_out_5, circuit_d_1_out_5, circuit_e_1_out_5,
       circuit_f_1_out_5, circuit_g_1_out_5;

  circuit_a circuit_a_1 (.A(A), .B(B), .C(C), .D(A), .out_5(circuit_a_1_out_5));
  circuit_b circuit_b_1 (.A(A), .B(B), .C(C), .D(A), .out_5(circuit_b_1_out_5));
  circuit_c circuit_c_1 (.A(A), .B(B), .C(C), .D(A), .out_5(circuit_c_1_out_5));
  circuit_d circuit_d_1 (.A(A), .B(B), .C(C), .D(A), .out_5(circuit_d_1_out_5));
  circuit_e circuit_e_1 (.A(A), .B(B), .C(C), .D(A), .out_5(circuit_e_1_out_5));
  circuit_f circuit_f_1 (.A(A), .B(B), .C(C), .D(A), .out_5(circuit_f_1_out_5));
  circuit_g circuit_g_1 (.A(A), .B(B), .C(C), .D(A), .out_5(circuit_g_1_out_5));
  _7_Segment_Display u_7_segment_display_1 (
    .g(circuit_g_1_out_5), .f(circuit_f_1_out_5), .a(circuit_a_1_out_5), .b(circuit_b_1_out_5),
    .e(circuit_e_1_out_5), .d(circuit_d_1_out_5), .c(circuit_c_1_out_5));  // open: dp

  assign D = A;

  // Notes on the sheet:
  //   BCD-to-seven-segment Converter
endmodule

module circuit_a (
  input  A,
  input  B,
  input  C,
  input  D,
  output out_5
);

  wire and_1_out, and_2_out, not_1_out, not_2_out, or_1_out, or_2_out;

  and and_1 (and_1_out, B, D);
  not not_1 (not_1_out, B);
  not not_2 (not_2_out, D);
  and and_2 (and_2_out, not_1_out, not_2_out);
  or or_1 (or_1_out, A, and_1_out);
  or or_2 (or_2_out, C, and_2_out);
  or or_3 (out_5, or_1_out, or_2_out);

  // Notes on the sheet:
  //   B'D' + BD + C + A
endmodule

module circuit_b (
  input  A,
  input  B,
  input  C,
  input  D,
  output out_5
);

  wire and_1_out, and_2_out, not_1_out, not_2_out, not_3_out, or_1_out;

  not not_1 (not_1_out, C);
  not not_2 (not_2_out, D);
  and and_1 (and_1_out, C, D);
  and and_2 (and_2_out, not_1_out, not_2_out);
  not not_3 (not_3_out, B);
  or or_1 (or_1_out, and_1_out, and_2_out);
  or or_2 (out_5, not_3_out, or_1_out);

  // Notes on the sheet:
  //   B' + C'D' + CD
endmodule

module circuit_c (
  input  A,
  input  B,
  input  C,
  input  D,
  output out_5
);

  wire not_1_out, or_1_out;

  not not_1 (not_1_out, C);
  or or_1 (or_1_out, B, not_1_out);
  or or_2 (out_5, or_1_out, D);

  // Notes on the sheet:
  //   C' + D + B
endmodule

module circuit_d (
  input  A,
  input  B,
  input  C,
  input  D,
  output out_5
);

  wire and_1_out, and_2_out, and_3_out, and_4_out, and_5_out, not_1_out, not_2_out, not_3_out, or_1_out,
       or_2_out, or_3_out;

  not not_1 (not_1_out, B);
  not not_2 (not_2_out, D);
  not not_3 (not_3_out, C);
  and and_1 (and_1_out, C, not_2_out);
  and and_2 (and_2_out, not_3_out, D);
  and and_3 (and_3_out, not_1_out, C);
  and and_4 (and_4_out, not_1_out, not_2_out);
  and and_5 (and_5_out, B, and_2_out);
  or or_1 (or_1_out, A, and_4_out);
  or or_2 (or_2_out, and_3_out, and_1_out);
  or or_3 (or_3_out, or_1_out, or_2_out);
  or or_4 (out_5, or_3_out, and_5_out);

  // Notes on the sheet:
  //   B'D' + B'C + CD' + BC'D + A
endmodule

module circuit_e (
  input  A,
  input  B,
  input  C,
  input  D,
  output out_5
);

  wire and_1_out, and_2_out, not_1_out, not_2_out;

  not not_1 (not_1_out, B);
  not not_2 (not_2_out, D);
  and and_1 (and_1_out, not_1_out, not_2_out);
  and and_2 (and_2_out, C, not_2_out);
  or or_1 (out_5, and_1_out, and_2_out);

  // Notes on the sheet:
  //   B'D' + CD'
endmodule

module circuit_f (
  input  A,
  input  B,
  input  C,
  input  D,
  output out_5
);

  wire and_1_out, and_2_out, and_3_out, not_1_out, not_2_out, or_1_out, or_2_out;

  not not_1 (not_1_out, C);
  not not_2 (not_2_out, D);
  and and_1 (and_1_out, B, not_1_out);
  and and_2 (and_2_out, B, not_2_out);
  and and_3 (and_3_out, not_1_out, not_2_out);
  or or_1 (or_1_out, A, and_1_out);
  or or_2 (or_2_out, and_2_out, and_3_out);
  or or_3 (out_5, or_1_out, or_2_out);

  // Notes on the sheet:
  //   A + BD' + BC' + C'D'
endmodule

module circuit_g (
  input  A,
  input  B,
  input  C,
  input  D,
  output out_5
);

  wire and_1_out, and_2_out, and_3_out, not_1_out, not_2_out, not_3_out, or_1_out, or_2_out;

  not not_1 (not_1_out, C);
  not not_2 (not_2_out, D);
  not not_3 (not_3_out, B);
  and and_1 (and_1_out, B, not_1_out);
  and and_2 (and_2_out, B, not_2_out);
  and and_3 (and_3_out, not_3_out, C);
  or or_1 (or_1_out, A, and_1_out);
  or or_2 (or_2_out, and_2_out, and_3_out);
  or or_3 (out_5, or_1_out, or_2_out);

  // Notes on the sheet:
  //   A + BC' + B'C + BD'
endmodule
