// Logisim project excessThree.circ as structural Verilog: 5 circuits, main circuit main
module main (
  input  Ain,
  input  Bin,
  input  Cin,
  input  Din,
  output Aout,
  output Bout,
  output Cout,
  output Dout
);

  circuit_1 circuit_1_1 (.A(Ain), .B(Bin), .C(Cin), .D(Din), .out_5(Aout));
  circuit_2 circuit_2_1 (.A(Ain), .B(Bin), .C(Cin), .D(Din), .out_5(Bout));
  circuit_3 circuit_3_1 (.A(Ain), .B(Bin), .C(Cin), .D(Din), .out_5(Cout));
  circuit_4 circuit_4_1 (.A(Ain), .B(Bin), .C(Cin), .D(Din), .out_5(Dout));

  // Notes on the sheet:
  //   BCD to Excess-3
endmodule

module circuit_1 (
  input  A,
  input  B,
  input  C,
  input  D,
  output out_5
);

  wire and_1_out, and_2_out, or_1_out;

  and and_1 (and_1_out, B, C);
  and and_2 (and_2_out, B, D);
  or or_1 (or_1_out, A, and_1_out);
  or or_2 (out_5, or_1_out, and_2_out);

  // Notes on the sheet:
  //   BD + BC + A
endmodule

module circuit_2 (
  input  A,
  input  B,
  input  C,
  input  D,
  output out_5
);

  wire and_1_out, and_2_out, and_3_out, and_4_out, not_1_out, not_2_out, not_3_out, or_1_out;

  not not_1 (not_1_out, C);
  not not_2 (not_2_out, B);
  and and_1 (and_1_out, B, not_1_out);
  and and_2 (and_2_out, not_2_out, C);
  not not_3 (not_3_out, D);
  and and_3 (and_3_out, not_2_out, D);
  and and_4 (and_4_out, and_1_out, not_3_out);
  or or_1 (or_1_out, and_2_out, and_3_out);
  or or_2 (out_5, and_4_out, or_1_out);

  // Notes on the sheet:
  //   B'C + B'D + BC'D'
endmodule

module circuit_3 (
  input  A,
  input  B,
  input  C,
  input  D,
  output out_5
);

  wire and_1_out, and_2_out, not_1_out, not_2_out;

  not not_1 (not_1_out, C);
  not not_2 (not_2_out, D);
  and and_1 (and_1_out, C, D);
  and and_2 (and_2_out, not_1_out, not_2_out);
  or or_1 (out_5, and_1_out, and_2_out);

  // Notes on the sheet:
  //   C'D' + CD
endmodule

module circuit_4 (
  input  A,
  input  B,
  input  C,
  input  D,
  output out_5
);

  not not_1 (out_5, D);

  // Notes on the sheet:
  //   D'
endmodule
