// Logisim project highLow.circ as structural Verilog: 1 circuit, main circuit main
module main (
  input  A,
  input  B,
  input  C,
  input  D,
  output out_5
);

  wire and_1_out, and_2_out, and_3_out, not_1_out, not_2_out, or_1_out;

  and and_1 (and_1_out, A, B);
  not not_1 (not_1_out, C);
  not not_2 (not_2_out, D);
  and and_2 (and_2_out, not_1_out, not_2_out);
  and and_3 (and_3_out, C, D);
  or or_1 (or_1_out, and_2_out, and_3_out);
  and and_4 (out_5, and_1_out, or_1_out);

  // Notes on the sheet:
  //   ABC'D' + ABCD
  //   A and B high, C and D both low or both high
endmodule
