// Logisim project alarmCircuit.circ as structural Verilog: 1 circuit, main circuit main
module main (
  input  A,
  input  B,
  input  C,
  input  D,
  output out_5
);

  wire and_1_out, and_2_out, and_3_out, or_1_out, or_2_out, or_3_out;

  or or_1 (or_1_out, D, C);
  and and_1 (and_1_out, C, D);
  or or_2 (or_2_out, or_1_out, B);
  and and_2 (and_2_out, B, or_1_out);
  and and_3 (and_3_out, A, or_2_out);
  or or_3 (or_3_out, and_2_out, and_1_out);
  or or_4 (out_5, and_3_out, or_3_out);

  // Notes on the sheet:
  //   AB + AC + AD + BC + BD +CD
  //   4 Switch Alarm Circuit Design
endmodule
