// Logisim project functionZ.circ as structural Verilog: 1 circuit, main circuit main
module main (
  input  A,
  input  B,
  input  C,
  input  D,
  output out_5
);

  wire AB_out, ABp_out, and_1_out, and_2_out, and_3_out, and_4_out, ApB_out, ApBp_out, CD_out, CDp_out,
       CpD_out, CpDp_out, not_1_out, not_2_out, not_3_out, not_4_out, or_1_out, or_2_out, or_3_out, or_4_out;

  not not_1 (not_1_out, A);
  not not_2 (not_2_out, B);
  not not_3 (not_3_out, C);
  not not_4 (not_4_out, D);
  and AB (AB_out, A, B);
  and ApB (ApB_out, not_1_out, B);
  and ABp (ABp_out, A, not_2_out);
  and ApBp (ApBp_out, not_2_out, not_1_out);
  and CpDp (CpDp_out, not_3_out, not_4_out);
  and CpD (CpD_out, not_3_out, D);
  and CDp (CDp_out, C, not_4_out);
  and CD (CD_out, C, D);
  or or_1 (or_1_out, CpD_out, CDp_out);
  or or_2 (or_2_out, CpDp_out, CD_out);
  and and_1 (and_1_out, AB_out, or_2_out);
  and and_2 (and_2_out, ApBp_out, or_2_out);
  and and_3 (and_3_out, ApB_out, or_1_out);
  and and_4 (and_4_out, or_1_out, ABp_out);
  or or_3 (or_3_out, and_1_out, and_2_out);
  or or_4 (or_4_out, and_3_out, and_4_out);
  or or_5 (out_5, or_3_out, or_4_out);

  // Notes on the sheet:
  //   Function Z
  //   A'B'C'D' + A'B'CD + A'BC'D + A'BCD' + ABC'D' + ABCD + AB'C'D + AB'CD'
endmodule
