// Logisim project 130_JK_BasicCombi.circ as structural Verilog: 7 circuits, main circuit half_adder
module half_adder (
  input  A,
  input  B,
  output Sum,
  output Carry
);

  xor xor_1 (Sum, A, B);
  and and_1 (Carry, A, B);
endmodule

module full_adder (
  input  A,
  input  B,
  input  Carry_in,
  output Sum,
  output Carry_out
);

  wire half_adder_1_carry, half_adder_1_sum, half_adder_2_carry;

  half_adder half_adder_1 (.A(A), .B(B), .Sum(half_adder_1_sum), .Carry(half_adder_1_carry));
  half_adder half_adder_2 (.A(half_adder_1_sum), .B(Carry_in), .Sum(Sum), .Carry(half_adder_2_carry));
  or or_1 (Carry_out, half_adder_1_carry, half_adder_2_carry);

  // Notes on the sheet:
  //   input 1: A
  //   input 2: B
  //   S = A O B
  //   C = AB
  //   input 1: A O B
  //   input 2: Cin
  //   S = A O B O C
  //   C = (A O B) Cin
endmodule

module ripple_carry_adder_4bit (
  input  A3,
  input  A2,
  input  A1,
  input  A0,
  input  B3,
  input  B2,
  input  B1,
  input  B0,
  output out_9,
  output out_10,
  output out_11,
  output out_12,
  output out_13
);

  wire full_adder0_carry_out, full_adder1_carry_out, full_adder2_carry_out;

  full_adder full_adder3 (.A(A3), .B(B3), .Carry_in(full_adder2_carry_out), .Sum(out_10), .Carry_out(out_9));
  full_adder full_adder2 (
    .A(A2), .B(B2), .Carry_in(full_adder1_carry_out), .Sum(out_11), .Carry_out(full_adder2_carry_out));
  full_adder full_adder1 (
    .A(A1), .B(B1), .Carry_in(full_adder0_carry_out), .Sum(out_12), .Carry_out(full_adder1_carry_out));
  full_adder full_adder0 (.A(A0), .B(B0), .Carry_in(1'b0), .Sum(out_13), .Carry_out(full_adder0_carry_out));
endmodule

module half_subtractor (
  input  A,
  input  y,
  output Difference,
  output Borrow
);

  wire not_1_out;

  xor xor_1 (Difference, A, y);
  not not_1 (not_1_out, A);
  and and_1 (Borrow, not_1_out, y);
endmodule

module full_subtractor (
  input  A,
  input  B,
  input  Borrow_in,
  output Difference,
  output Borrow_out
);

  wire half_subtractor_1_borrow, half_subtractor_1_difference, half_subtractor_2_borrow;

  half_subtractor half_subtractor_1 (
    .A(A), .y(B), .Difference(half_subtractor_1_difference), .Borrow(half_subtractor_1_borrow));
  half_subtractor half_subtractor_2 (
    .A(half_subtractor_1_difference), .y(Borrow_in), .Difference(Difference),
    .Borrow(half_subtractor_2_borrow));
  or or_1 (Borrow_out, half_subtractor_1_borrow, half_subtractor_2_borrow);
endmodule

module twos_comp_subtractor_4bit (
  input  A3,
  input  A2,
  input  A1,
  input  A0,
  input  B3,
  input  B2,
  input  B1,
  input  B0,
  output out_9,
  output out_10,
  output out_11,
  output out_12,
  output out_13
);

  wire full_subtractor_1_borrow_out, full_subtractor_2_borrow_out, full_subtractor_3_borrow_out,
       full_subtractor_4_borrow_out;

  full_subtractor full_subtractor_1 (
    .A(A3), .B(B3), .Borrow_in(full_subtractor_2_borrow_out), .Difference(out_10),
    .Borrow_out(full_subtractor_1_borrow_out));
  full_subtractor full_subtractor_2 (
    .A(A2), .B(B2), .Borrow_in(full_subtractor_3_borrow_out), .Difference(out_11),
    .Borrow_out(full_subtractor_2_borrow_out));
  full_subtractor full_subtractor_3 (
    .A(A1), .B(B1), .Borrow_in(full_subtractor_4_borrow_out), .Difference(out_12),
    .Borrow_out(full_subtractor_3_borrow_out));
  full_subtractor full_subtractor_4 (
    .A(A0), .B(B0), .Borrow_in(1'b0), .Difference(out_13), .Borrow_out(full_subtractor_4_borrow_out));
  not not_1 (out_9, full_subtractor_1_borrow_out);

  // Notes on the sheet:
  //   If the leftmost bit is 1, final answer is positive and in binary. Neglect leftmost bit.
  //   If the leftmost bit is 0, final answer is negative and in 2's complement.
endmodule

module multiplication_4bit (
  input  A0,
  input  A1,
  input  A2,
  input  A3,
  input  B0,
  input  B1,
  input  B2,
  input  B3,
  output P0,
  output P1,
  output P2,
  output P3,
  output P4,
  output P5,
  output P6,
  output P7
);

  wire and_2_out, and_3_out, and_4_out, and_5_out, and_6_out, and_7_out, and_8_out, and_9_out, and_10_out,
       and_11_out, and_12_out, and_13_out, and_14_out, and_15_out, and_16_out, full_adder_1_carry_out,
       full_adder_1_sum, full_adder_2_carry_out, full_adder_2_sum, full_adder_3_carry_out, full_adder_3_sum,
       full_adder_4_carry_out, full_adder_4_sum, full_adder_5_carry_out, full_adder_5_sum,
       full_adder_6_carry_out, full_adder_7_carry_out, half_adder_1_carry, half_adder_2_carry,
       half_adder_2_sum, half_adder_3_carry, half_adder_4_carry;

  and and_1 (P0, B0, A0);
  and and_2 (and_2_out, B1, A0);
  and and_3 (and_3_out, B2, A0);
  and and_4 (and_4_out, B3, A0);
  and and_5 (and_5_out, B0, A1);
  and and_6 (and_6_out, B1, A1);
  and and_7 (and_7_out, B2, A1);
  and and_8 (and_8_out, B3, A1);
  half_adder half_adder_1 (.A(and_5_out), .B(and_2_out), .Sum(P1), .Carry(half_adder_1_carry));
  full_adder full_adder_1 (
    .A(and_6_out), .B(and_3_out), .Carry_in(half_adder_1_carry), .Sum(full_adder_1_sum),
    .Carry_out(full_adder_1_carry_out));
  full_adder full_adder_2 (
    .A(and_7_out), .B(and_4_out), .Carry_in(full_adder_1_carry_out), .Sum(full_adder_2_sum),
    .Carry_out(full_adder_2_carry_out));
  half_adder half_adder_2 (
    .A(and_8_out), .B(full_adder_2_carry_out), .Sum(half_adder_2_sum), .Carry(half_adder_2_carry));
  and and_9 (and_9_out, B0, A2);
  and and_10 (and_10_out, B1, A2);
  and and_11 (and_11_out, B2, A2);
  and and_12 (and_12_out, B3, A2);
  half_adder half_adder_3 (.A(and_9_out), .B(full_adder_1_sum), .Sum(P2), .Carry(half_adder_3_carry));
  full_adder full_adder_3 (
    .A(and_10_out), .B(full_adder_2_sum), .Carry_in(half_adder_3_carry), .Sum(full_adder_3_sum),
    .Carry_out(full_adder_3_carry_out));
  full_adder full_adder_4 (
    .A(and_11_out), .B(half_adder_2_sum), .Carry_in(full_adder_3_carry_out), .Sum(full_adder_4_sum),
    .Carry_out(full_adder_4_carry_out));
  full_adder full_adder_5 (
    .A(and_12_out), .B(half_adder_2_carry), .Carry_in(full_adder_4_carry_out), .Sum(full_adder_5_sum),
    .Carry_out(full_adder_5_carry_out));
  and and_13 (and_13_out, B0, A3);
  and and_14 (and_14_out, B1, A3);
  and and_15 (and_15_out, B2, A3);
  and and_16 (and_16_out, B3, A3);
  half_adder half_adder_4 (.A(and_13_out), .B(full_adder_3_sum), .Sum(P3), .Carry(half_adder_4_carry));
  full_adder full_adder_6 (
    .A(and_14_out), .B(full_adder_4_sum), .Carry_in(half_adder_4_carry), .Sum(P4),
    .Carry_out(full_adder_6_carry_out));
  full_adder full_adder_7 (
    .A(and_15_out), .B(full_adder_5_sum), .Carry_in(full_adder_6_carry_out), .Sum(P5),
    .Carry_out(full_adder_7_carry_out));
  full_adder full_adder_8 (
    .A(and_16_out), .B(full_adder_5_carry_out), .Carry_in(full_adder_7_carry_out), .Sum(P6), .Carry_out(P7));

  // Notes on the sheet:
  //   Note: Index [0] is rightmost
endmodule
