// Logisim project 130_JK_FullAdderBreadboard.circ as structural Verilog: 1 circuit, main circuit full_adder
module full_adder (
  input  A,
  input  B,
  input  C,
  output Sum,
  output Carry
);

  wire A_xor_B_out, AB_out, ABp_out, and_1_out, and_2_out, and_3_out, ApB_out, not_1_out, not_2_out,
       not_3_out, not_4_out;

  not not_1 (not_1_out, B);
  not not_2 (not_2_out, A);
  and ABp (ABp_out, A, not_1_out);
  and ApB (ApB_out, B, not_2_out);
  and AB (AB_out, B, A);
  or A_xor_B (A_xor_B_out, ABp_out, ApB_out);
  not not_3 (not_3_out, C);
  not not_4 (not_4_out, A_xor_B_out);
  and and_1 (and_1_out, A_xor_B_out, not_3_out);
  and and_2 (and_2_out, not_4_out, C);
  and and_3 (and_3_out, A_xor_B_out, C);
  or or_1 (Sum, and_1_out, and_2_out);
  or or_2 (Carry, and_3_out, AB_out);

  // Notes on the sheet:
  //   Full adder implementation using IC 7404, 7408, 7432
endmodule
